// Digital circuit 4 Bit PC Adder.dig as structural Verilog
module _4_Bit_PC_Adder (
  input  [3:0] I__3_0,
  output [3:0] O__3_0
);

  Add #(.Bits(4)) add_1 (.a(I__3_0), .b(4'b0001), .c_i(1'b0), .s(O__3_0));  // open: c_o

  // Other names for the same wires on the sheet: I[3:0] = I__3_0; O[3:0] = O__3_0
endmodule
