// Digital circuit 4 Bit PC Reg.dig as structural Verilog
module _4_Bit_PC_Reg (
  input  [3:0] I__3_0,
  input  CLK,
  output [3:0] O__3_0
);

  _1_Bit_Reg _1_bit_reg_1 (.Din(I__3_0[3]), .Sel(1'b1), .CLK(CLK), .Dout(O__3_0[3]));
  _1_Bit_Reg _1_bit_reg_2 (.Din(I__3_0[2]), .Sel(1'b1), .CLK(CLK), .Dout(O__3_0[2]));
  _1_Bit_Reg _1_bit_reg_3 (.Din(I__3_0[1]), .Sel(1'b1), .CLK(CLK), .Dout(O__3_0[1]));
  _1_Bit_Reg _1_bit_reg_4 (.Din(I__3_0[0]), .Sel(1'b1), .CLK(CLK), .Dout(O__3_0[0]));

  // Other names for the same wires on the sheet: B0 = O__3_0[0]; B1 = O__3_0[1]; B2 = O__3_0[2]; B3 = O__3_0[3];
  //   A0 = I__3_0[0]; A1 = I__3_0[1]; A2 = I__3_0[2]; A3 = I__3_0[3]
endmodule
