// Digital circuit 6 Bit ALU.dig as structural Verilog
module _6_Bit_ALU (
  input  [5:0] A_5_0,
  input  [5:0] B_5_0,
  input  [1:0] Op_1_0,
  output [5:0] R_5_0
);

  wire [5:0] _6bitadder_1_r_5_0, _6bitand_1_r_5_0, _6bitrotate_1_r_5_0;

  _6BitAdder _6bitadder_1 (.A_5_0(A_5_0), .B_5_0(B_5_0), .R_5_0(_6bitadder_1_r_5_0));  // open: Cout
  _6BitAnd _6bitand_1 (.A_5_0(A_5_0), .B_5_0(B_5_0), .R_5_0(_6bitand_1_r_5_0));
  _6BitRotate _6bitrotate_1 (.A_5_0(A_5_0), .B_5_0(B_5_0), .R_5_0(_6bitrotate_1_r_5_0));
  Multiplexer #(.Selector_Bits(2), .Bits(6)) multiplexer_1 (
    .sel(Op_1_0), .in_0(_6bitadder_1_r_5_0), .in_1(_6bitand_1_r_5_0), .in_2(_6bitrotate_1_r_5_0),
    .in_3({6{1'b0}}), .out(R_5_0));

  // Other names for the same wires on the sheet: A[5:0] = A_5_0; B[5:0] = B_5_0
endmodule
