// Digital circuit 6 Bit CPU.dig as structural Verilog
module _6_Bit_CPU (
  input  [15:0] WRD_15_0,
  input  [3:0] WR__3_0,
  input  WE,
  input  CLK,
  input  PC_En,
  input  [3:0] RA2__3_0,
  output [15:0] RD2__15_0,
  output [5:0] R_5_0
);

  wire CPU_CLK, Imm_Sel, JMP_Sel, WE_t;
  wire [1:0] Op, R2;
  wire [3:0] _4_bit_pc_adder_1_o__3_0, _4_bit_pc_reg_1_o__3_0, JMP_Level, multiplexer_1_out, Opcode;
  wire [5:0] Dont_Care, multiplexer_2_out, register_set_1_a_5_0, register_set_1_b_5_0;

  Multiplexer #(.Bits(4)) multiplexer_1 (
    .sel(JMP_Sel), .in_0(_4_bit_pc_adder_1_o__3_0), .in_1(JMP_Level), .out(multiplexer_1_out));
  _4_Bit_PC_Adder _4_bit_pc_adder_1 (.I__3_0(_4_bit_pc_reg_1_o__3_0), .O__3_0(_4_bit_pc_adder_1_o__3_0));
  _4_Bit_PC_Reg _4_bit_pc_reg_1 (.I__3_0(multiplexer_1_out), .CLK(CPU_CLK), .O__3_0(_4_bit_pc_reg_1_o__3_0));
  and and_1 (CPU_CLK, PC_En, CLK);
  _10_x_16_RAM _10_x_16_ram_1 (
    .RA1__3_0(_4_bit_pc_reg_1_o__3_0), .RA2__3_0(RA2__3_0), .WR__3_0(WR__3_0), .WRD_15_0(WRD_15_0), .WE(WE),
    .CLK(CLK), .RD1_15_0({Opcode, JMP_Level, R2, Dont_Care}), .RD2_15_0(RD2__15_0));
  Register_Set register_set_1 (
    .WE(WE_t), .WRD_5_0(R_5_0), .WR__2_0(JMP_Level[3:1]), .CLK(CPU_CLK), .RA_2_0(JMP_Level[3:1]),
    .RB_2_0({JMP_Level[0], R2}), .A_5_0(register_set_1_a_5_0), .B_5_0(register_set_1_b_5_0));
  Control_Logic control_logic_1 (.Opcode__3_0(Opcode), .Op__1_0(Op), .WE(WE_t), .Imm_Sel(Imm_Sel), .JMP_Sel(JMP_Sel));
  _6_Bit_ALU _6_bit_alu_1 (.A_5_0(register_set_1_a_5_0), .B_5_0(multiplexer_2_out), .Op_1_0(Op), .R_5_0(R_5_0));
  Multiplexer #(.Bits(6)) multiplexer_2 (
    .sel(Imm_Sel), .in_0(register_set_1_b_5_0), .in_1({JMP_Level[0], R2, Dont_Care[5:3]}),
    .out(multiplexer_2_out));

  // Other names for the same wires on the sheet: R2[2] = JMP_Level[0]; R1[2:0] = JMP_Level[3:1];
  //   RD2[15:0] = RD2__15_0

  // Notes on the sheet:
  //   WR__3_0: SELECT ROW OF RAM
  //   6 BIT CPU
  //   =============================================
  //   REG Mode (00) = 2 Bit (Type of OP) + 2 Bit (Operation) + 3 Bit (Reg 1) + 3 Bit (Reg 2) + 6 Bit unused
  //   Imm Mode (01) = 2 Bit (Type of OP) + 2 Bit (Operation) + 3 Bit (Reg 1) + 6 bit data + 3 Bit unsed
  //   OP CODES
  //   =============
  //   ADD = 00
  //   AND = 01
  //   ROR = 10
  //   JMP = 10 00
  //   JL = 10 01
  //   AND R1,R1 =  0001001001000000
  //   ADD R1, 5 = 0100001000101000
  //   JMP 0001 = 1000000100000000
endmodule
