// Digital circuit 6BitAdder.dig as structural Verilog
module _6BitAdder (
  input  [5:0] A_5_0,
  input  [5:0] B_5_0,
  output [5:0] R_5_0,
  output Cout
);

  wire fa_2_cout, fa_3_cout, fa_4_cout, fa_5_cout, fa_6_cout;

  FA fa_1 (.Y(B_5_0[5]), .X(A_5_0[5]), .Cin(fa_2_cout), .Cout(Cout), .S(R_5_0[5]));
  FA fa_2 (.Y(B_5_0[4]), .X(A_5_0[4]), .Cin(fa_3_cout), .Cout(fa_2_cout), .S(R_5_0[4]));
  FA fa_3 (.Y(B_5_0[3]), .X(A_5_0[3]), .Cin(fa_4_cout), .Cout(fa_3_cout), .S(R_5_0[3]));
  FA fa_4 (.Y(B_5_0[2]), .X(A_5_0[2]), .Cin(fa_5_cout), .Cout(fa_4_cout), .S(R_5_0[2]));
  FA fa_5 (.Y(B_5_0[1]), .X(A_5_0[1]), .Cin(fa_6_cout), .Cout(fa_5_cout), .S(R_5_0[1]));
  FA fa_6 (.Y(B_5_0[0]), .X(A_5_0[0]), .Cin(1'b0), .Cout(fa_6_cout), .S(R_5_0[0]));

  // Other names for the same wires on the sheet: x0 = A_5_0[0]; x1 = A_5_0[1]; x2 = A_5_0[2]; x3 = A_5_0[3];
  //   x4 = A_5_0[4]; x5 = A_5_0[5]; y0 = B_5_0[0]; y1 = B_5_0[1]; y2 = B_5_0[2]; y3 = B_5_0[3]; y4 = B_5_0[4];
  //   y5 = B_5_0[5]; s0 = R_5_0[0]; s1 = R_5_0[1]; s2 = R_5_0[2]; s3 = R_5_0[3]; s4 = R_5_0[4]; s5 = R_5_0[5]
endmodule
