// Digital circuit Control Logic.dig as structural Verilog
module Control_Logic (
  input  [3:0] Opcode__3_0,
  output [1:0] Op__1_0,
  output WE,
  output Imm_Sel,
  output JMP_Sel
);

  wire and_1_out, not_1_out, not_2_out, not_3_out, not_4_out, not_5_out, not_6_out;

  not not_1 (not_1_out, Opcode__3_0[3]);
  and and_1 (and_1_out, Opcode__3_0[2], Opcode__3_0[3]);
  and and_2 (Imm_Sel, Opcode__3_0[2], not_1_out);
  not not_2 (not_2_out, Opcode__3_0[0]);
  not not_3 (not_3_out, Opcode__3_0[1]);
  not not_4 (not_4_out, Opcode__3_0[2]);
  and and_3 (JMP_Sel, not_2_out, not_3_out, not_4_out, Opcode__3_0[3]);
  not not_5 (not_5_out, and_1_out);
  not not_6 (not_6_out, JMP_Sel);
  and and_4 (WE, not_6_out, not_5_out);

  assign Op__1_0 = Opcode__3_0[1:0];

  // Other names for the same wires on the sheet: JMP = JMP_Sel
endmodule
